# Fritzing sketch TeensyL293D (saved by Fritzing 0.9.2b)
breadboards: 1

parts:
  Teensy_3_1 = Teensy 3.0  # not connected
  IC1 = L293D [package=THT]
  VCC1 = 4 x AAA Battery Mount
  M1 = DC Motor
  M2 = DC Motor
  J1 = female pin header, 6 pins [form="♀ (female)"]  # not connected

nets:
  N1: IC1.Out_1_(_Controlled_by_Enable_1_), M2.pin_2
  N2: IC1.0V, VCC1.-
  N3: IC1.Out_2_(_Controlled_by_Enable_1_), M2.pin_1
  N4: IC1.+Vmotor, IC1.+V, VCC1.+
  N5: IC1.Out_3_(_Controlled_by_Enable_2_), M1.pin_2
  N6: IC1.Out_4_(_Controlled_by_Enable_2_), M1.pin_1

notes:
  The 6 Headers are for 3 IR sensors, and 3 Photodiodes.
  +V should be between 4.5v & 7v
