# Fritzing sketch FubarinoMiniLCD (saved by Fritzing 0.9.2b)
breadboards: 1

parts:
  IC1 = Fubarino Mini v1.5 [package="DIP (Dual Inline) [THT]"]
  J2 = female pin header, 20 pins [form="♀ (female)"]
  J1 = female pin header, 20 pins [form="♀ (female)"]
  LCD1 = LCD screen
  J3 = male pin header, 16 pins [form="♂ (male)"]
  R1 = Resistor [tolerance=±5% resistance=220 package=THT]
  R2 = TRIMPOT [package=trimpot_pth_s3_lock]

nets:
  N1: IC1.Vout, J2.pin1
  GND: IC1.GND, J2.pin2, J1.pin2, LCD1.VSS, LCD1.R/W, LCD1.LED-, J3.pin1, J3.pin12, J3.pin16, R2.CW
  N2: IC1.3.3V, J2.pin3, J1.pin3
  N3: IC1.Pin_0/A0, J2.pin4
  N4: IC1.Pin_1, J2.pin5
  N5: IC1.Pin_2, J2.pin6
  N6: IC1.Pinl_3/A1, J2.pin7
  N7: IC1.Pin_4/A2, J2.pin8
  N8: IC1.Pin_5/A3, J2.pin9
  N9: IC1.Pin_6/A4, J2.pin10
  N10: IC1.Pin_7/A5, J2.pin11
  N11: IC1.Pin_8/A6, IC1.RB1/PGC, J2.pin12
  N12: IC1.Pin_9/A7, IC1.RB0/PGD, J2.pin13
  N13: IC1.Pin_10/A8, J2.pin14
  N14: IC1.Pinl_11/A9, J2.pin15
  N15: IC1.Pin_12/A10, J2.pin16
  N16: IC1.Pin_13/A11, J2.pin17
  N17: IC1.Pin_14, J2.pin18
  N18: IC1.Pin_15, J2.pin19
  N19: IC1.Pin_16, J2.pin20
  N20: IC1.Pin_17, J1.pin20
  N21: IC1.Pin_18, J1.pin19
  N22: IC1.Pin_19, J1.pin18
  N23: IC1.Pin_20/A12, J1.pin17
  N24: IC1.Pin_21, J1.pin16
  N25: IC1.Pin_22, J1.pin15
  N26: IC1.Pin_23, J1.pin14
  N27: IC1.Pin_24, J1.pin13
  N28: IC1.Pin_25, J1.pin12
  N29: IC1.Pin_26, J1.pin11
  N30: IC1.Pin_27, J1.pin10, LCD1.RS, J3.pin13
  N31: IC1.Pin_28, J1.pin9, LCD1.E, J3.pin11
  N32: IC1.Pin_29, J1.pin8, LCD1.DB4, J3.pin6
  N33: IC1.Pin_30, J1.pin7, LCD1.DB5, J3.pin5
  N34: IC1.Pin_31, J1.pin6, LCD1.DB6, J3.pin4
  N35: IC1.Pin_32, J1.pin5, LCD1.DB7, J3.pin3
  N36: IC1.N.C., J1.pin4
  VIN: IC1.Vin, J1.pin1, LCD1.VDD, J3.pin15, R1.Pin_0, R2.CCW
  N37: LCD1.V0, J3.pin14, R2.WIPER
  N38: LCD1.DB0, J3.pin10
  N39: LCD1.DB1, J3.pin9
  N40: LCD1.DB2, J3.pin8
  N41: LCD1.DB3, J3.pin7
  N42: LCD1.LED+, J3.pin2, R1.Pin_1

custom parts:
  Fubarino Mini v1.5: A chipKIT PIC32 based development board from Schmalz Haus LLC.
