# Fritzing sketch FubarinoMiniLCDFullSize (saved by Fritzing 0.9.2b)
breadboards: 1

parts:
  IC1 = Fubarino Mini v1.5 [package="DIP (Dual Inline) [THT]"]
  J2 = female pin header, 20 pins [form="♀ (female)"]
  J1 = female pin header, 20 pins [form="♀ (female)"]
  LCD1 = LCD screen
  J3 = male pin header, 16 pins [form="♂ (male)"]  # not connected
  R2 = TRIMPOT [package=trimpot_pth_s3_lock]
  R3 = Resistor [tolerance=±5% resistance=220 package=THT]

nets:
  N1: IC1.Vout, J2.pin1
  N2: IC1.GND, J2.pin2, J1.pin2
  N3: IC1.3.3V, J2.pin3, J1.pin3
  N4: IC1.Pin_0/A0, J2.pin4
  N5: IC1.Pin_1, J2.pin5
  N6: IC1.Pin_2, J2.pin6
  N7: IC1.Pinl_3/A1, J2.pin7
  N8: IC1.Pin_4/A2, J2.pin8
  N9: IC1.Pin_5/A3, J2.pin9
  N10: IC1.Pin_6/A4, J2.pin10
  N11: IC1.Pin_7/A5, J2.pin11
  N12: IC1.Pin_8/A6, IC1.RB1/PGC, J2.pin12
  N13: IC1.Pin_9/A7, IC1.RB0/PGD, J2.pin13
  N14: IC1.Pin_10/A8, J2.pin14
  N15: IC1.Pinl_11/A9, J2.pin15
  N16: IC1.Pin_12/A10, J2.pin16
  N17: IC1.Pin_13/A11, J2.pin17
  N18: IC1.Pin_14, J2.pin18
  N19: IC1.Pin_15, J2.pin19
  N20: IC1.Pin_16, J2.pin20
  N21: IC1.Pin_17, J1.pin20
  N22: IC1.Pin_18, J1.pin19
  N23: IC1.Pin_19, J1.pin18
  N24: IC1.Pin_20/A12, J1.pin17
  N25: IC1.Pin_21, J1.pin16
  N26: IC1.Pin_22, J1.pin15
  N27: IC1.Pin_23, J1.pin14
  N28: IC1.Pin_24, J1.pin13
  N29: IC1.Pin_25, J1.pin12
  N30: IC1.Pin_26, J1.pin11
  N31: IC1.Pin_27, J1.pin10
  N32: IC1.Pin_28, J1.pin9
  N33: IC1.Pin_29, J1.pin8
  N34: IC1.Pin_30, J1.pin7
  N35: IC1.Pin_31, J1.pin6
  N36: IC1.Pin_32, J1.pin5
  N37: IC1.N.C., J1.pin4
  N38: IC1.Vin, J1.pin1
  N39: LCD1.VSS, LCD1.R/W, LCD1.DB2, LCD1.LED-, R2.CCW
  N40: LCD1.VDD, R2.CW, R3.Pin_1
  N41: LCD1.V0, R2.WIPER
  N42: LCD1.LED+, R3.Pin_0

custom parts:
  Fubarino Mini v1.5: A chipKIT PIC32 based development board from Schmalz Haus LLC.
