# Fritzing sketch FubarinoMiniOneWire (saved by Fritzing 0.9.2b)

parts:
  J1 = female pin header, 14 pins [form="♀ (female)"]
  J2 = female pin header, 14 pins [form="♀ (female)"]
  J3 = female pin header, 14 pins [form="♀ (female)"]
  R1 = Resistor [tolerance=±5% resistance=4.7k package=THT]
  U1 = TMP36 [package=to-92-kit]  # not connected
  U2 = TMP36 [package=to-92-kit]  # not connected
  U3 = TMP36 [package=to-92-kit]  # not connected
  IC1 = Fubarino Mini v1.5 [package="DIP (Dual Inline) [THT]"]

nets:
  N1: J1.pin2, R1.Pin_1
  N2: J1.pin3, IC1.3.3V
  N3: J2.pin1, IC1.GND
  N4: J3.pin1, R1.Pin_0
  N5: J3.pin4, IC1.Pin_2

custom parts:
  Fubarino Mini v1.5: A chipKIT PIC32 based development board from Schmalz Haus LLC.
