# Fritzing sketch FubarinoSDOneWire (saved by Fritzing 0.9.2b)

parts:
  FubarinoSD1 = Fubarino SD [chip_label=FubarinoSD package="DIP (Dual Inline) [THT]"]
  J1 = female pin header, 14 pins [form="♀ (female)"]
  J2 = female pin header, 14 pins [form="♀ (female)"]
  J3 = female pin header, 14 pins [form="♀ (female)"]
  R1 = Resistor [tolerance=±5% resistance=4.7k package=THT]
  U1 = TMP36 [package=to-92-kit]  # not connected
  U2 = TMP36 [package=to-92-kit]  # not connected
  U3 = TMP36 [package=to-92-kit]  # not connected

nets:
  N1: FubarinoSD1.GND, J2.pin1
  N2: FubarinoSD1.3.3V, J1.pin3
  N3: FubarinoSD1.Digital2, J3.pin4
  N4: J1.pin2, R1.Pin_1
  N5: J3.pin1, R1.Pin_0

custom parts:
  Fubarino SD: Fubarino SD, v1.5, a chipKIT board.
