# Fritzing sketch FubarinoMinishiftRegister (saved by Fritzing 0.9.2b)
breadboards: 1

parts:
  U1 = 74HC595 [package="DIP16 [THT]"]
  LED1 = LED - 5mm [color="Red (633nm)" package="5 mm [THT]"]
  LED2 = LED - 5mm [color="Red (633nm)" package="5 mm [THT]"]
  LED3 = LED - 5mm [color="Red (633nm)" package="5 mm [THT]"]
  LED4 = LED - 5mm [color="Red (633nm)" package="5 mm [THT]"]
  LED5 = LED - 5mm [color="Red (633nm)" package="5 mm [THT]"]
  LED6 = LED - 5mm [color="Red (633nm)" package="5 mm [THT]"]
  LED7 = LED - 5mm [color="Red (633nm)" package="5 mm [THT]"]
  LED8 = LED - 5mm [color="Red (633nm)" package="5 mm [THT]"]
  R1 = Resistor [tolerance=±5% resistance=220 package=THT]
  R2 = Resistor [tolerance=±5% resistance=220 package=THT]
  R3 = Resistor [tolerance=±5% resistance=220 package=THT]
  R4 = Resistor [tolerance=±5% resistance=220 package=THT]
  R5 = Resistor [tolerance=±5% resistance=220 package=THT]
  R6 = Resistor [tolerance=±5% resistance=220 package=THT]
  R7 = Resistor [tolerance=±5% resistance=220 package=THT]
  R8 = Resistor [tolerance=±5% resistance=220 package=THT]
  IC1 = Fubarino Mini v1.5 [package="DIP (Dual Inline) [THT]"]
  J3 = female pin header, 20 pins [form="♀ (female)"]
  J4 = female pin header, 20 pins [form="♀ (female)"]

nets:
  N1: U1.Q1, R8.Pin_1
  N2: U1.Q2, R7.Pin_1
  N3: U1.Q3, R6.Pin_1
  N4: U1.Q4, R5.Pin_1
  N5: U1.Q5, R1.Pin_1
  N6: U1.Q6, R4.Pin_1
  N7: U1.Q7, R3.Pin_1
  N8: U1.Q7', R2.Pin_1
  N9: LED1.cathode, LED2.cathode, LED3.cathode, LED4.cathode, LED5.cathode, LED6.cathode, LED7.cathode, LED8.cathode
  N10: LED1.anode, R6.Pin_0
  N11: LED2.anode, R5.Pin_0
  N12: LED3.anode, R7.Pin_0
  N13: LED4.anode, R1.Pin_0
  N14: LED5.anode, R3.Pin_0
  N15: LED6.anode, R2.Pin_0
  N16: LED7.anode, R4.Pin_0
  N17: LED8.anode, R8.Pin_0
  N18: IC1.Vout, J3.pin1
  N19: IC1.GND, J3.pin2, J4.pin2
  N20: IC1.3.3V, J3.pin3, J4.pin3
  N21: IC1.Pin_0/A0, J3.pin4
  N22: IC1.Pin_1, J3.pin5
  N23: IC1.Pin_2, J3.pin6
  N24: IC1.Pinl_3/A1, J3.pin7
  N25: IC1.Pin_4/A2, J3.pin8
  N26: IC1.Pin_5/A3, J3.pin9
  N27: IC1.Pin_6/A4, J3.pin10
  N28: IC1.Pin_7/A5, J3.pin11
  N29: IC1.Pin_8/A6, IC1.RB1/PGC, J3.pin12
  N30: IC1.Pin_9/A7, IC1.RB0/PGD, J3.pin13
  N31: IC1.Pin_10/A8, J3.pin14
  N32: IC1.Pinl_11/A9, J3.pin15
  N33: IC1.Pin_12/A10, J3.pin16
  N34: IC1.Pin_13/A11, J3.pin17
  N35: IC1.Pin_14, J3.pin18
  N36: IC1.Pin_15, J3.pin19
  N37: IC1.Pin_16, J3.pin20
  N38: IC1.Pin_17, J4.pin20
  N39: IC1.Pin_18, J4.pin19
  N40: IC1.Pin_19, J4.pin18
  N41: IC1.Pin_20/A12, J4.pin17
  N42: IC1.Pin_21, J4.pin16
  N43: IC1.Pin_22, J4.pin15
  N44: IC1.Pin_23, J4.pin14
  N45: IC1.Pin_24, J4.pin13
  N46: IC1.Pin_25, J4.pin12
  N47: IC1.Pin_26, J4.pin11
  N48: IC1.Pin_27, J4.pin10
  N49: IC1.Pin_28, J4.pin9
  N50: IC1.Pin_29, J4.pin8
  N51: IC1.Pin_30, J4.pin7
  N52: IC1.Pin_31, J4.pin6
  N53: IC1.Pin_32, J4.pin5
  N54: IC1.N.C., J4.pin4
  N55: IC1.Vin, J4.pin1

custom parts:
  Fubarino Mini v1.5: A chipKIT PIC32 based development board from Schmalz Haus LLC.
