# Fritzing sketch FubarinoSDshiftRegister (saved by Fritzing 0.9.2b)
breadboards: 1

parts:
  FubarinoSD1 = Fubarino SD [chip_label=FubarinoSD package="DIP (Dual Inline) [THT]"]  # not connected
  U1 = 74HC595 [package="DIP16 [THT]"]
  J1 = female pin header, 28 pins [form="♀ (female)"]
  J2 = female pin header, 28 pins [form="♀ (female)"]
  J3 = female pin header, 8 pins [form="♀ (female)"]  # not connected
  LED1 = LED - 5mm [color="Red (633nm)" package="5 mm [THT]"]
  LED2 = LED - 5mm [color="Red (633nm)" package="5 mm [THT]"]
  LED3 = LED - 5mm [color="Red (633nm)" package="5 mm [THT]"]
  LED4 = LED - 5mm [color="Red (633nm)" package="5 mm [THT]"]
  LED5 = LED - 5mm [color="Red (633nm)" package="5 mm [THT]"]
  LED6 = LED - 5mm [color="Red (633nm)" package="5 mm [THT]"]
  LED7 = LED - 5mm [color="Red (633nm)" package="5 mm [THT]"]
  LED8 = LED - 5mm [color="Red (633nm)" package="5 mm [THT]"]
  R1 = Resistor [tolerance=±5% resistance=220 package=THT]
  R2 = Resistor [tolerance=±5% resistance=220 package=THT]
  R3 = Resistor [tolerance=±5% resistance=220 package=THT]
  R4 = Resistor [tolerance=±5% resistance=220 package=THT]
  R5 = Resistor [tolerance=±5% resistance=220 package=THT]
  R6 = Resistor [tolerance=±5% resistance=220 package=THT]
  R7 = Resistor [tolerance=±5% resistance=220 package=THT]
  R8 = Resistor [tolerance=±5% resistance=220 package=THT]

nets:
  N1: U1.Q1, R8.Pin_1
  N2: U1.Q2, R7.Pin_1
  N3: U1.Q3, R6.Pin_1
  N4: U1.Q4, R5.Pin_1
  N5: U1.Q5, R1.Pin_1
  N6: U1.Q6, R4.Pin_1
  N7: U1.Q7, R3.Pin_1
  N8: U1.GND, J2.pin2
  N9: U1.Q7', R2.Pin_1
  N10: U1.SH_CP, J2.pin7
  N11: U1.ST_CP, J2.pin6
  N12: U1.DS, J2.pin5
  N13: U1.VCC, J1.pin3
  N14: LED1.cathode, LED2.cathode, LED3.cathode, LED4.cathode, LED5.cathode, LED6.cathode, LED7.cathode, LED8.cathode
  N15: LED1.anode, R6.Pin_0
  N16: LED2.anode, R5.Pin_0
  N17: LED3.anode, R7.Pin_0
  N18: LED4.anode, R1.Pin_0
  N19: LED5.anode, R3.Pin_0
  N20: LED6.anode, R2.Pin_0
  N21: LED7.anode, R4.Pin_0
  N22: LED8.anode, R8.Pin_0

custom parts:
  Fubarino SD: Fubarino SD, v1.5, a chipKIT board.
