# Fritzing sketch FubarinoMinRGB (saved by Fritzing 0.9.2b)
breadboards: 1

parts:
  R1 = Rotary Potentiometer (Small) [maximum_resistance=100kΩ package=THT]
  IC1 = Fubarino Mini v1.5 [package="DIP (Dual Inline) [THT]"]  # not connected
  LED1 = RGB LED (com. cathode, rgb) [package="5 mm [THT]"]

nets:
  N1: R1.leg1, LED1.red_anode

notes:
  int val = 0;
  //potentiometer is A0
  void setup() {
  Serial.begin(9600);
  }
  void loop() {
  val = analogRead(A0);
  Serial.println(val);
  delay(15);
  }
  setup() {
  pinMode(4, OUTPUT);
  pinMode(5, OUTPUT);
  pinMode(6, OUTPUT);
  }
  void loop() {
  for (int ii = 0; ii < 256; ii++)
  {
  digitalWrite(4, ii);
  digitalWrite(5, ii);
  digitalWrite(6, ii);
  }
  delay(500);
  }

custom parts:
  Fubarino Mini v1.5: A chipKIT PIC32 based development board from Schmalz Haus LLC.
