# Fritzing sketch FubarinoMiniPotLED (saved by Fritzing 0.9.2b)
breadboards: 1

parts:
  R1 = Rotary Potentiometer (Small) [maximum_resistance=100kΩ package=THT]
  IC1 = Fubarino Mini v1.5 [package="DIP (Dual Inline) [THT]"]  # not connected
  LED1 = LED - 5mm [color="Red (633nm)" package="5 mm [THT]"]
  R2 = Resistor [tolerance=±5% resistance=220 package=THT]

nets:
  N1: R1.leg1, R2.Pin_1
  N2: LED1.cathode, R2.Pin_0

custom parts:
  Fubarino Mini v1.5: A chipKIT PIC32 based development board from Schmalz Haus LLC.
