# Fritzing sketch FubarinoSDPotLED (saved by Fritzing 0.9.2b)
breadboards: 1

parts:
  R1 = Rotary Potentiometer (Small) [maximum_resistance=100kΩ package=THT]
  LED1 = LED - 5mm [color="Red (633nm)" package="5 mm [THT]"]
  FubarinoSD1 = Fubarino SD [chip_label=FubarinoSD package="DIP (Dual Inline) [THT]"]
  R2 = Resistor [tolerance=±5% resistance=220 package=THT]

nets:
  N1: R1.wiper, FubarinoSD1.Analog0
  N2: R1.leg2, R2.Pin_1
  N3: LED1.cathode, R2.Pin_0

custom parts:
  Fubarino SD: Fubarino SD, v1.5, a chipKIT board.
