# Fritzing sketch Untitled Sketch 2 (saved by Fritzing 0.9.2b)
breadboards: 1

parts:
  Teensy_3_1 = Teensy 3.1  # not connected
  R1 = Resistor [tolerance=±5% resistance=220 package=THT]
  LED1 = LED - 5mm [color="Red (633nm)" package="5 mm [THT]"]
  LED2 = LED - 5mm [color="Blue (525nm)" package="5 mm [THT]"]
  R2 = Resistor [tolerance=±5% resistance=4.7k package=THT]

nets:
  N1: R1.Pin_0, LED1.anode
  N2: R1.Pin_1, R2.Pin_1
  N3: LED2.anode, R2.Pin_0

notes:
  LED Pin 14s
  IR Photodiode pin 17
  code:
  void setup() {
  pinMode(14, OUTPUT);
  pinMode(17, INPUT);
  digitalWrite(14, HIGH);
  Serial.begin(9600);
  }
  void loop() {
  int val = analogRead(A3);
  Serial.println(val);
  }s
