# Fritzing sketch FubarinoMiniDotStarWiring (saved by Fritzing 0.9.2b)
breadboards: 1

parts:
  IC1 = Fubarino Mini v1.5 [package="DIP (Dual Inline) [THT]"]  # not connected
  LPD8806_RGB_LED_Strip2 = LPD8806 RGB LED Strip
  Power_plug1 = Power plug

nets:
  N1: LPD8806_RGB_LED_Strip2.GND#4, Power_plug1.GND
  +5V: LPD8806_RGB_LED_Strip2.+5V, Power_plug1.VCC

custom parts:
  Fubarino Mini v1.5: A chipKIT PIC32 based development board from Schmalz Haus LLC.
  LPD8806 RGB LED Strip: Digitally addressable RGB LED strip
