# Fritzing sketch FubarinoSDDotStarWiring (saved by Fritzing 0.9.2b)
breadboards: 1

parts:
  LPD8806_RGB_LED_Strip2 = LPD8806 RGB LED Strip
  Power_plug1 = Power plug
  FubarinoSD1 = Fubarino SD [chip_label=FubarinoSD package="DIP (Dual Inline) [THT]"]  # not connected

nets:
  N1: LPD8806_RGB_LED_Strip2.GND#4, Power_plug1.GND
  +5V: LPD8806_RGB_LED_Strip2.+5V, Power_plug1.VCC

custom parts:
  LPD8806 RGB LED Strip: Digitally addressable RGB LED strip
  Fubarino SD: Fubarino SD, v1.5, a chipKIT board.
